# Fritzing sketch Nano_Music_Buzzer (saved by Fritzing 0.9.3b)
breadboards: 1

parts:
  Part1 = Arduino Nano (Rev3.0) (ICSP)
  J1 = Piezo Speaker
  S1 = Pushbutton [package="[THT]"]
  Q1 = NPN-Transistor [package="TO92 [THT]"]
  R1 = Resistor [tolerance=±5% resistance=47 package=THT]

nets:
  N1: Part1.GND, J1.pin1, S1.Pin_1, S1.Pin_2, Q1.E
  N2: Part1.D4, S1.Pin_3, S1.Pin_4
  N3: Part1.D8, R1.Pin_0
  N4: J1.pin2, Q1.C
  N5: Q1.B, R1.Pin_1
